# Fritzing sketch perler_tool (saved by Fritzing 0.9.3b)
breadboards: 1
perfboards: 1

parts:
  Raspberry_Pi_1 = Raspberry Pi 3 [part_number=RPI-3-V1.2]
  CameraLight = LEDs [package=led10mm]
  R4 = Resistor [tolerance=±5% resistance=220 package="2010 [SMD]"]
  J1 = Basic Servo
  M1 = DC Motor
  Mosfet_driver_module1 = IFR520 MOS module [package=THT]
  External_5v = 2.1mm Barrel Jack with Terminal Block
  MOTOR1 = Adafruit Gear-Reduced Stepper Motor (small)  # not connected
  X1 = X113647 Stepper Driver Board [package=board]
  D2F1 = D2F-FL Omron Snap Action Limit Switch with Level
  R5 = Resistor [tolerance=±5% resistance=10k package="2010 [SMD]"]
  External_5v1 = 2.1mm Barrel Jack with Terminal Block  # not connected
  J2 = Camdenboss CTB0158-2 [part_number=CTB0158-2 package=THT]  # not connected
  J3 = Camdenboss CTB0158-2 [part_number=CTB0158-2 package=THT]
  J4 = Camdenboss CTB0158-2 [part_number=CTB0158-2 package=THT]
  J5 = Camdenboss CTB0158-2 [part_number=CTB0158-2 package=THT]
  J6 = Camdenboss CTB0158-2 [part_number=CTB0158-2 package=THT]
  M2 = DC Motor
  X2 = X113647 Stepper Driver Board [package=board]
  J7 = Basic Servo
  Raspberry_Pi_2 = Raspberry Pi 3 [part_number=RPI-3-V1.2]
  R6 = Resistor [tolerance=±5% resistance=220 package="2010 [SMD]"]
  Mosfet_driver_module2 = IFR520 MOS module [package=THT]
  J8 = Camdenboss CTB0158-2 [part_number=CTB0158-2 package=THT]
  J10 = Camdenboss CTB0158-2 [part_number=CTB0158-2 package=THT]
  R7 = Resistor [tolerance=±5% resistance=10k package="2010 [SMD]"]
  J11 = Camdenboss CTB0158-2 [part_number=CTB0158-2 package=THT]  # not connected

nets:
  N1: Raspberry_Pi_1.GPIO5, X1.IN1
  N2: Raspberry_Pi_1.GPIO6, X1.IN2
  N3: Raspberry_Pi_1.GPIO13, X1.IN4
  N4: Raspberry_Pi_1.GPIO12, X1.IN3
  N5: Raspberry_Pi_1.ID_SC, R4.Pin_1, J1.vcc, Mosfet_driver_module1.pin6, External_5v.POS, D2F1.COM, D2F1.NO, R5.Pin_1
  N6: Raspberry_Pi_1.GPIO24, Mosfet_driver_module1.pin1
  N7: Raspberry_Pi_1.GPIO23, J1.pulse
  N8: Raspberry_Pi_1.GND, Mosfet_driver_module1.pin3
  N9: Raspberry_Pi_1.5V, Mosfet_driver_module1.pin2
  N10: CameraLight.C, J1.gnd, Mosfet_driver_module1.pin7, External_5v.NEG, R5.Pin_0
  N11: CameraLight.A, R4.Pin_0
  N12: M1.pin_1, Mosfet_driver_module1.pin4
  N13: M1.pin_2, Mosfet_driver_module1.pin5
  N14: J3.pin1, J4.pin1, J5.pin1, J6.pin1, R7.Pin_0
  N15: J3.pin2, J4.pin2, J5.pin2, R6.Pin_1, J10.pin2, R7.Pin_1
  N16: J3.terminal_1, Mosfet_driver_module2.pin7
  N17: J3.terminal_2, Mosfet_driver_module2.pin6
  N18: J4.terminal_1, J7.gnd
  N19: J4.terminal_2, J7.vcc
  N20: J5.terminal_1, X2.GND
  N21: J5.terminal_2, X2.+V
  N22: J6.pin2, R6.Pin_0
  N23: M2.pin_1, Mosfet_driver_module2.pin4
  N24: M2.pin_2, Mosfet_driver_module2.pin5
  N25: X2.IN1, Raspberry_Pi_2.GPIO5
  N26: X2.IN2, Raspberry_Pi_2.GPIO6
  N27: X2.IN3, Raspberry_Pi_2.GPIO12
  N28: X2.IN4, Raspberry_Pi_2.GPIO13
  N29: J7.pulse, Raspberry_Pi_2.GPIO23
  N30: Raspberry_Pi_2.ID_SC, J10.pin1
  N31: Raspberry_Pi_2.GPIO24, Mosfet_driver_module2.pin1
  N32: Raspberry_Pi_2.GND, J8.terminal_1
  N33: Raspberry_Pi_2.5V, J8.terminal_2

custom parts:
  IFR520 MOS module: Breakout board for the IFR520 MOSFET transistor. The module is designed to switch heavy DC loads from a single digital pin of your microcontroller. Its main purpose is to provide a low cost way to drive a DC motor for robotics applications, but the module can be used to control most high current DC loads. Screw terminals are provided to interface to your load and external power source. An LED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
  Adafruit Gear-Reduced Stepper Motor (small): Adafruit gear-reduction stepper motor (small)
  X113647 Stepper Driver Board: A common stepper motor driver board based on ULN2003APG darlington array
  D2F-FL Omron Snap Action Limit Switch with Level: Snap action switch with stainless steel lever.
