# Fritzing sketch perler_tool_b (saved by Fritzing 0.9.3b)
perfboards: 1

parts:
  M3 = Stepper Motor - Bipolar  # not connected
  12v = 2.1mm Barrel Jack with Terminal Block
  J13 = Camdenboss CTB0158-2 [part_number=CTB0158-2 package=THT]
  LM1 = RioRand LM2596
  BIGTREETECH_TMC2209_V1_1 = TMC2209  # not connected
  Raspberry_Pi_3 = Raspberry Pi 3 [part_number=RPI-3-V1.2]
  J14 = Camdenboss CTB0158-2 [part_number=CTB0158-2 package=THT]
  Part1 = USB Type A Female Breakout Board [part_number=BOB-12700]
  J18 = Camdenboss CTB0158-2 [part_number=CTB0158-2 package=THT]
  X3 = X113647 Stepper Driver Board [package=board]
  J19 = Camdenboss CTB0158-2 [part_number=CTB0158-2 package=THT]  # not connected
  D2F5 = D2F-FL Omron Snap Action Limit Switch with Level
  J20 = Camdenboss CTB0158-2 [part_number=CTB0158-2 package=THT]
  J22 = Camdenboss CTB0158-2 [part_number=CTB0158-2 package=THT]
  MOTOR1 = Adafruit Gear-Reduced Stepper Motor (small)  # not connected
  Part2 = USB Type A Female Breakout Board [part_number=BOB-12700]
  LED1 = smd LED [color="Red (633nm)" package="1206 [SMD]"]  # not connected

nets:
  N1: 12v.POS, J13.terminal_1
  N2: 12v.NEG, J13.terminal_2
  N3: J13.pin1, X3.+V
  N4: J13.pin2, X3.GND
  VCC: LM1.Pin_2, Part1.VCC, Part2.VCC
  GND: LM1.Pin_3, Part1.GND, Part2.GND
  N5: Raspberry_Pi_3.GPIO5, X3.IN1
  N6: Raspberry_Pi_3.GPIO6, X3.IN2
  N7: Raspberry_Pi_3.GPIO13, X3.IN4
  N8: Raspberry_Pi_3.GPIO21, J20.terminal_1
  N9: Raspberry_Pi_3.GPIO20, J22.terminal_1
  N10: Raspberry_Pi_3.GPIO16, J22.terminal_2
  N11: Raspberry_Pi_3.GPIO12, X3.IN3
  N12: Raspberry_Pi_3.GPIO25, J14.pin2
  N13: Raspberry_Pi_3.GND, J18.terminal_1
  N14: Raspberry_Pi_3.5V, J18.terminal_2
  N15: J14.terminal_1, D2F5.COM
  N16: J14.terminal_2, D2F5.NO

custom parts:
  TMC2209: This is a Stepper Motor Controller for integrated circuits.
  USB Type A Female Breakout Board: USB breakout board for a Type A connector. sparkfun.com
  X113647 Stepper Driver Board: A common stepper motor driver board based on ULN2003APG darlington array
  D2F-FL Omron Snap Action Limit Switch with Level: Snap action switch with stainless steel lever.
  Adafruit Gear-Reduced Stepper Motor (small): Adafruit gear-reduction stepper motor (small)
