# Fritzing sketch perler_v_filter (saved by Fritzing 0.9.4)
perfboards: 1

parts:
  Part1 = Adafruit Metro Mini [part_number="Adafruit #2590"]  # not connected
  J1 = Basic Servo
  Part2 = Flora TCS34725 Color Sensor  # not connected
  M1 = Dagu DGServo 9g (Top view) [part_number=RS001B]
  JACK1 = 2.1mm Barrel Jack with Terminal Block  # not connected

nets:
  GND: J1.gnd, M1.gnd
  VCC: J1.vcc, M1.vcc

custom parts:
  Adafruit Metro Mini: We sure love the ATmega328 here at Adafruit, and we use them a lot for our own projects. The processor has plenty of GPIO, Analog inputs, hardware UART SPI and I2C, timers and PWM galore - just enough for most simple projects. When we need to go small, we use a Pro Trinket 3V or 5V, but if you want to have USB-to-Serial built in, we reach for an Adafruit METRO Mini. METRO Mini is the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
  Flora TCS34725 Color Sensor: Your electronics can now see in dazzling color with this lovely color light sensor. We found the best color sensor on the market, the TCS34725, which has RGB and Clear light sensing elements. An IR blocking filter, integrated on-chip and localized to the color sensing photodiodes, minimizes the IR spectral component of the incoming light and allows color measurements to be made accurately. The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
